// Logisim project cpu_risc_v.circ as structural Verilog
module main (
);

  Register #(.width(32)) register_1 ();  // open: D, en, clk, Q, clr
  interger_register_file interger_register_file_1 ();  // open: Clock, EnableWrite, SetRegister, Data, ReadRegisterY, ReadRegisterX, EnableRead, OutputY, OutputX
endmodule

module interger_register_file (
  input  Clock,
  input  EnableWrite,
  input  [3:0] ReadRegisterY,
  input  EnableRead,
  input  [3:0] ReadRegisterX,
  input  [3:0] SetRegister,
  input  [31:0] Data,
  output [31:0] OutputY,
  output [31:0] OutputX
);

  wire decoder_1_out0, decoder_1_out1, decoder_1_out2, decoder_1_out3, decoder_1_out4, decoder_1_out5,
       decoder_1_out6, decoder_1_out7, decoder_1_out8, decoder_1_out9, decoder_1_out10, decoder_1_out11,
       decoder_1_out12, decoder_1_out13, decoder_1_out14, decoder_1_out15, ER0_out, ER1_out, ER2_out,
       ER3_out, ER4_out, ER5_out, ER6_out, ER7_out, ER8_out, ER9_out, ER10_out, ER11_out, ER12_out, ER13_out,
       ER14_out, ER15_out;
  wire [31:0] demultiplexer_1_out0, demultiplexer_1_out1, demultiplexer_1_out2, demultiplexer_1_out3,
       demultiplexer_1_out4, demultiplexer_1_out5, demultiplexer_1_out6, demultiplexer_1_out7,
       demultiplexer_1_out8, demultiplexer_1_out9, demultiplexer_1_out10, demultiplexer_1_out11,
       demultiplexer_1_out12, demultiplexer_1_out13, demultiplexer_1_out14, demultiplexer_1_out15,
       register_1_q, register_2_q, register_3_q, register_4_q, register_5_q, register_6_q, register_7_q,
       register_8_q, register_9_q, register_10_q, register_11_q, register_12_q, register_13_q, register_14_q,
       register_15_q, register_16_q;

  Decoder #(.enable("false"), .select(4)) decoder_1 (
    .out0(decoder_1_out0), .out1(decoder_1_out1), .out2(decoder_1_out2), .out3(decoder_1_out3),
    .out4(decoder_1_out4), .out5(decoder_1_out5), .out6(decoder_1_out6), .out7(decoder_1_out7),
    .out8(decoder_1_out8), .out9(decoder_1_out9), .out10(decoder_1_out10), .out11(decoder_1_out11),
    .out12(decoder_1_out12), .out13(decoder_1_out13), .out14(decoder_1_out14), .out15(decoder_1_out15),
    .sel(SetRegister));
  and ER0 (ER0_out, EnableWrite, decoder_1_out0);
  and ER1 (ER1_out, EnableWrite, decoder_1_out1);
  and ER2 (ER2_out, EnableWrite, decoder_1_out2);
  and ER3 (ER3_out, EnableWrite, decoder_1_out3);
  and ER4 (ER4_out, EnableWrite, decoder_1_out4);
  and ER5 (ER5_out, EnableWrite, decoder_1_out5);
  and ER6 (ER6_out, EnableWrite, decoder_1_out6);
  and ER7 (ER7_out, EnableWrite, decoder_1_out7);
  and ER8 (ER8_out, EnableWrite, decoder_1_out8);
  and ER9 (ER9_out, EnableWrite, decoder_1_out9);
  and ER10 (ER10_out, EnableWrite, decoder_1_out10);
  and ER11 (ER11_out, EnableWrite, decoder_1_out11);
  and ER12 (ER12_out, EnableWrite, decoder_1_out12);
  and ER13 (ER13_out, EnableWrite, decoder_1_out13);
  and ER14 (ER14_out, EnableWrite, decoder_1_out14);
  and ER15 (ER15_out, EnableWrite, decoder_1_out15);
  Register #(.width(32)) register_1 (
    .D(demultiplexer_1_out0), .en(ER0_out), .Q(register_1_q), .clk(Clock));  // open: clr
  Register #(.width(32)) register_2 (
    .D(demultiplexer_1_out1), .en(ER1_out), .Q(register_2_q), .clk(Clock));  // open: clr
  Register #(.width(32)) register_3 (
    .D(demultiplexer_1_out2), .en(ER2_out), .Q(register_3_q), .clk(Clock));  // open: clr
  Register #(.width(32)) register_4 (
    .D(demultiplexer_1_out3), .en(ER3_out), .Q(register_4_q), .clk(Clock));  // open: clr
  Register #(.width(32)) register_5 (
    .D(demultiplexer_1_out4), .en(ER4_out), .Q(register_5_q), .clk(Clock));  // open: clr
  Register #(.width(32)) register_6 (
    .D(demultiplexer_1_out5), .en(ER5_out), .Q(register_6_q), .clk(Clock));  // open: clr
  Register #(.width(32)) register_7 (
    .D(demultiplexer_1_out6), .en(ER6_out), .Q(register_7_q), .clk(Clock));  // open: clr
  Register #(.width(32)) register_8 (
    .D(demultiplexer_1_out7), .en(ER7_out), .Q(register_8_q), .clk(Clock));  // open: clr
  Demultiplexer #(.select(4), .width(32)) demultiplexer_1 (
    .out0(demultiplexer_1_out0), .out1(demultiplexer_1_out1), .out2(demultiplexer_1_out2),
    .out3(demultiplexer_1_out3), .out4(demultiplexer_1_out4), .out5(demultiplexer_1_out5),
    .out6(demultiplexer_1_out6), .out7(demultiplexer_1_out7), .out8(demultiplexer_1_out8),
    .out9(demultiplexer_1_out9), .out10(demultiplexer_1_out10), .out11(demultiplexer_1_out11),
    .out12(demultiplexer_1_out12), .out13(demultiplexer_1_out13), .out14(demultiplexer_1_out14),
    .out15(demultiplexer_1_out15), .in(Data), .sel(SetRegister));
  Register #(.width(32)) register_9 (
    .D(demultiplexer_1_out8), .en(ER8_out), .Q(register_9_q), .clk(Clock));  // open: clr
  Register #(.width(32)) register_10 (
    .D(demultiplexer_1_out9), .en(ER9_out), .Q(register_10_q), .clk(Clock));  // open: clr
  Register #(.width(32)) register_11 (
    .D(demultiplexer_1_out10), .en(ER10_out), .Q(register_11_q), .clk(Clock));  // open: clr
  Register #(.width(32)) register_12 (
    .D(demultiplexer_1_out11), .en(ER11_out), .Q(register_12_q), .clk(Clock));  // open: clr
  Register #(.width(32)) register_13 (
    .D(demultiplexer_1_out12), .en(ER12_out), .Q(register_13_q), .clk(Clock));  // open: clr
  Register #(.width(32)) register_14 (
    .D(demultiplexer_1_out13), .en(ER13_out), .Q(register_14_q), .clk(Clock));  // open: clr
  Register #(.width(32)) register_15 (
    .D(demultiplexer_1_out14), .en(ER14_out), .Q(register_15_q), .clk(Clock));  // open: clr
  Register #(.width(32)) register_16 (
    .D(demultiplexer_1_out15), .en(ER15_out), .Q(register_16_q), .clk(Clock));  // open: clr
  Multiplexer #(.enable("true"), .select(4), .width(32)) multiplexer_1 (
    .in0(register_1_q), .in1(register_2_q), .in2(register_3_q), .in3(register_4_q), .in4(register_5_q),
    .in5(register_6_q), .in6(register_7_q), .in7(register_8_q), .in8(register_9_q), .in9(register_10_q),
    .in10(register_11_q), .in11(register_12_q), .in12(register_13_q), .in13(register_14_q),
    .in14(register_15_q), .in15(register_16_q), .out(OutputY), .sel(ReadRegisterY), .en(EnableRead));
  Multiplexer #(.enable("true"), .select(4), .width(32)) multiplexer_2 (
    .in0(register_1_q), .in1(register_2_q), .in2(register_3_q), .in3(register_4_q), .in4(register_5_q),
    .in5(register_6_q), .in6(register_7_q), .in7(register_8_q), .in8(register_9_q), .in9(register_10_q),
    .in10(register_11_q), .in11(register_12_q), .in12(register_13_q), .in13(register_14_q),
    .in14(register_15_q), .in15(register_16_q), .out(OutputX), .sel(ReadRegisterX), .en(EnableRead));
endmodule

module fp_register_file (
);

  Register #(.width(32)) register_1 ();  // open: D, en, clk, Q, clr
  Register #(.width(32)) register_2 ();  // open: D, en, clk, Q, clr
  Register #(.width(32)) register_3 ();  // open: D, en, clk, Q, clr
  Register #(.width(32)) register_4 ();  // open: D, en, clk, Q, clr
  Register #(.width(32)) register_5 ();  // open: D, en, clk, Q, clr
  Register #(.width(32)) register_6 ();  // open: D, en, clk, Q, clr
  Register #(.width(32)) register_7 ();  // open: D, en, clk, Q, clr
  Register #(.width(32)) register_8 ();  // open: D, en, clk, Q, clr
  Register #(.width(32)) register_9 ();  // open: D, en, clk, Q, clr
  Register #(.width(32)) register_10 ();  // open: D, en, clk, Q, clr
  Register #(.width(32)) register_11 ();  // open: D, en, clk, Q, clr
  Register #(.width(32)) register_12 ();  // open: D, en, clk, Q, clr
endmodule

module vector_register (
  input  WriteEnable,
  input  [31:0] Input_0,
  input  Clock,
  input  [31:0] Input_1,
  input  [31:0] Input_2,
  input  ReadEnable,
  output [31:0] Output_0,
  output [31:0] Output_1,
  output [31:0] Output_2
);

  Register #(.width(32)) v_sub_0 (.D(Input_0), .en(WriteEnable), .clk(Clock), .Q(Output_0), .clr(ReadEnable));
  Register #(.width(32)) v_sub_1 (.D(Input_1), .en(WriteEnable), .clk(Clock), .Q(Output_1), .clr(ReadEnable));
  Register #(.width(32)) v_sub_2 (.D(Input_2), .en(WriteEnable), .clk(Clock), .Q(Output_2), .clr(ReadEnable));
endmodule

module int_opcode_identifier (
  input  [6:0] Opcode,
  output IsIntOperation
);

  wire ALI_out, ALR_out, AUIPC_out, BRANCH_out, ECB_out, FENCE_out, JAL_out, JALR_out, LOAD_out, LUI_out,
       STORE_out;

  and LUI (LUI_out, Opcode[0], Opcode[1], Opcode[2], ~Opcode[3], Opcode[4], Opcode[5], ~Opcode[6]);  // AND_Gate
  and AUIPC (AUIPC_out, Opcode[0], Opcode[1], Opcode[2], ~Opcode[3], Opcode[4], ~Opcode[5], ~Opcode[6]);  // AND_Gate
  and JAL (JAL_out, Opcode[0], Opcode[1], Opcode[2], Opcode[3], ~Opcode[4], Opcode[5], Opcode[6]);  // AND_Gate
  and JALR (JALR_out, Opcode[0], Opcode[1], Opcode[2], ~Opcode[3], ~Opcode[4], Opcode[5], Opcode[6]);  // AND_Gate
  and BRANCH (BRANCH_out, Opcode[0], Opcode[1], ~Opcode[2], ~Opcode[3], ~Opcode[4], Opcode[5], Opcode[6]);  // AND_Gate
  and LOAD (LOAD_out, Opcode[0], Opcode[1], ~Opcode[2], ~Opcode[3], ~Opcode[4], ~Opcode[5], ~Opcode[6]);  // AND_Gate
  and STORE (STORE_out, Opcode[0], Opcode[1], ~Opcode[2], ~Opcode[3], ~Opcode[4], Opcode[5], ~Opcode[6]);  // AND_Gate
  and ALI (ALI_out, Opcode[0], Opcode[1], ~Opcode[2], ~Opcode[3], Opcode[4], ~Opcode[5], ~Opcode[6]);  // AND_Gate
  and ALR (ALR_out, Opcode[0], Opcode[1], ~Opcode[2], ~Opcode[3], Opcode[4], Opcode[5], ~Opcode[6]);  // AND_Gate
  and FENCE (FENCE_out, Opcode[0], Opcode[1], Opcode[2], Opcode[3], ~Opcode[4], ~Opcode[5], ~Opcode[6]);  // AND_Gate
  and ECB (ECB_out, Opcode[0], Opcode[1], ~Opcode[2], ~Opcode[3], Opcode[4], Opcode[5], Opcode[6]);  // AND_Gate
  or or_1 (IsIntOperation, LUI_out, AUIPC_out, JAL_out, JALR_out, BRANCH_out, LOAD_out, STORE_out, ALI_out, ALR_out, FENCE_out, ECB_out);

  // Notes on the sheet:
  //   Arithmetic-Logic operation with Immediate
  //   Arithmetic-Logic operations with register
endmodule
